# Fritzing sketch esp_doorbell (saved by Fritzing 0.9.3b)
stripboards: 1

parts:
  J1 = Camdenboss CTB0158-2 [part_number=CTB0158-2 package=THT]
  VCC1 = Battery
  U1 = Voltage Regulator - 3.3V [package="TO220 [THT]"]
  C1 = Tantalum Capacitor [capacitance=1μF package="100 mil [THT, tantalum]"]
  U2 = ESP8266 WiFi Module [part_number=ESP8266]
  R1 = Resistor [tolerance=±5% resistance=10k package=THT]
  R2 = Resistor [tolerance=±5% resistance=1.5k package=THT]
  J2 = female pin header, 2 pins [form="♀ (female)"]
  J3 = female pin header, 3 pins [form="♀ (female)"]
  J4 = female pin header, 2 pins [form="♀ (female)"]
  U3 = Optocoupler [package=THT]

nets:
  N1: J1.pin1, U2.RXD, U2.REST, R2.Pin_1, J2.pin1, U3.Pin_2, U3.Pin_5
  N2: J1.pin2, R1.Pin_0
  GND: VCC1.-, U1.GND, C1.-, U2.GND, U2.GPIO_15, J3.pin2, J4.pin2, U3.Pin_3, U3.Pin_4
  N3: VCC1.+, U1.input_voltage
  N4: U1.output_voltage, C1.+, U2.VCC, U2.GPIO_0, U2.CH_PD, R2.Pin_0, J3.pin1, J4.pin1
  N5: U2.TXD, R1.Pin_1, J2.pin2, U3.Pin_1, U3.Pin_6
  N6: U2.GPIO_12, J3.pin3
